# Fritzing sketch MainSketch (saved by Fritzing 0.7.12b)
breadboards: 1

parts:
  Arduino1 = Arduino
  LED1 = LED - 5mm [color="Red (633nm)" package="5 mm [THT]"]
  LED2 = LED - 5mm [color="Red (633nm)" package="5 mm [THT]"]
  LED3 = LED - 5mm [color="Red (633nm)" package="5 mm [THT]"]
  RGB = RGB LED (com. anode, rbg) [package="5 mm [THT]"]
  220 = Resistor [tolerance=±5% resistance=220 package=THT]
  220_2 = Resistor [tolerance=±5% resistance=220 package=THT]
  220_3 = Resistor [tolerance=±5% resistance=220 package=THT]
  10k = Resistor [tolerance=±5% resistance=10k package=THT]
  10k_2 = Resistor [tolerance=±5% resistance=10k package=THT]
  10k_3 = Resistor [tolerance=±5% resistance=10k package=THT]
  S1 = Pushbutton [package="[THT]"]
  S2 = Pushbutton [package="[THT]"]
  S3 = Pushbutton [package="[THT]"]
  150x2 = Resistor [tolerance=±5% resistance=150 package=THT]
  R2 = Resistor [tolerance=±5% resistance=150 package=THT]
  220_4 = Resistor [tolerance=±5% resistance=220 package=THT]  # not connected
  J1 = Piezo Speaker

nets:
  N1: Arduino1.D12, R2.Pin_1
  N2: Arduino1.D11, 150x2.Pin_1
  N3: Arduino1.D10, J1.pin1
  N4: Arduino1.D8, 10k.Pin_1, S1.Pin_3, S1.Pin_4
  N5: Arduino1.D7, 10k_2.Pin_1, S2.Pin_3, S2.Pin_4
  N6: Arduino1.D6, 10k_3.Pin_1, S3.Pin_3, S3.Pin_4
  N7: Arduino1.D4, 220_2.Pin_1
  N8: Arduino1.D3, 220.Pin_1
  N9: Arduino1.D2, 220_3.Pin_1
  N10: Arduino1.+5V, S1.Pin_1, S1.Pin_2, S2.Pin_1, S2.Pin_2, S3.Pin_1, S3.Pin_2
  N11: Arduino1.GND, LED1.cathode, LED2.cathode, LED3.cathode, RGB.common_anode, 10k.Pin_0, 10k_2.Pin_0, 10k_3.Pin_0, J1.pin2
  N12: LED1.anode, 220_2.Pin_0
  N13: LED2.anode, 220.Pin_0
  N14: LED3.anode, 220_3.Pin_0
  N15: RGB.blue_cathode, R2.Pin_0
  N16: RGB.green_cathode, 150x2.Pin_0
